# Fritzing sketch dht (saved by Fritzing 0.9.3b)
breadboards: 1

parts:
  Arduino_Uno_R3 = Arduino Uno (Rev3)
  EXTERNAL = Power Jack [part_number="POWER 5V" package=power_jack_smd]  # not connected
  R6 = Resistor [tolerance=±5% resistance=10k package=THT]
  DHT11 = DHT11 Humitidy and Temperature Sensor

nets:
  5V: Arduino_Uno_R3.D10_PWM/SS, Arduino_Uno_R3.5V, R6.Pin_0, DHT11.VDD
  GND: Arduino_Uno_R3.GND, DHT11.GND
  N1: R6.Pin_1, DHT11.DATA

custom parts:
  DHT11 Humitidy and Temperature Sensor: DHT11 Humidity and Temperature Sensor
