# Fritzing sketch ldr (saved by Fritzing 0.9.3b)
breadboards: 1

parts:
  Arduino_Uno_R3 = Arduino Uno (Rev3)
  EXTERNAL = Power Jack [part_number="POWER 5V" package=power_jack_smd]  # not connected
  LM393 = FC-28 Soil Hygrometer Module
  LDR = Photocell (LDR) [package=THT]

nets:
  N1: Arduino_Uno_R3.D12/MISO, LM393.DO
  5V: Arduino_Uno_R3.5V, LM393.VCC
  GND: Arduino_Uno_R3.GND, LM393.GND
  N2: LM393.POS, LDR.pin_1
  N3: LM393.NEG, LDR.pin_0

custom parts:
  FC-28 Soil Hygrometer Module: The FC-28 is a soil hygrometer module that uses the Texas Instruments LM393 comparator chip to provide an analog measurement of soil humidity. The digital output is high when soil moisture is over a certain threshold, as determined by adjusting the potentiometer.
