# Fritzing sketch mos (saved by Fritzing 0.9.3b)
breadboards: 1

parts:
  Arduino_Uno_R3 = Arduino Uno (Rev3)
  EXTERNAL = Power Jack [part_number="POWER 5V" package=power_jack_smd]  # not connected
  FC-28 = Soil Moisture Sensor [part_number="SOIL MOISTURE SENSOR"]
  LM393 = FC-28 Soil Hygrometer Module

nets:
  N1: Arduino_Uno_R3.A0, LM393.AO
  5V: Arduino_Uno_R3.5V, LM393.VCC
  GND: Arduino_Uno_R3.GND, LM393.GND
  N2: FC-28.SIG, LM393.NEG
  N3: FC-28.VCC, LM393.POS

custom parts:
  FC-28 Soil Hygrometer Module: The FC-28 is a soil hygrometer module that uses the Texas Instruments LM393 comparator chip to provide an analog measurement of soil humidity. The digital output is high when soil moisture is over a certain threshold, as determined by adjusting the potentiometer.
